// Logisim project riscv.circ as structural Verilog: 6 circuits, main circuit main
module main (
);

  wire ADD, ADI, ALU_ENABLE, AND, ANI, CLK, COUNTER_CLEAR, HLT, IR_ENABLE, LOAD, MEM_READ, MEM_WRITE, MOV,
       MUX_STORE_SELECT, MUXB_ENABLE, MUXB_SELECT, MUXMEM_SELECT, MUXY_ENABLE, MUXY_SELECT, MVI, OR, ORI,
       PC_ENABLE, PC_STOP, RA_ENABLE, RA_ENABLE_SELECT, RB_ENABLE, RB_ENABLE_SELECT, RM_ENABLE, RY_ENABLE,
       RY_ENABLE_SELECT, RZ_ENABLE, STAGE_1, STAGE_2, STAGE_3, STAGE_4, STAGE_5, STORE, SUB, SUI;
  wire [2:0] ALU__SELECT;
  wire [3:0] OPCODE;

  LED led_1 (.in(STAGE_2));
  LED led_2 (.in(STAGE_3));
  LED led_3 (.in(STAGE_1));
  LED led_4 (.in(STAGE_5));
  LED led_5 (.in(STAGE_4));
  CU cu_1 (
    .CLK(CLK), .MOV(MOV), .RA_ENABLE(RA_ENABLE), .ALU_ENABLE(ALU_ENABLE), .OPCODE(OPCODE), .MVI(MVI),
    .RB_ENABLE(RB_ENABLE), .ALU_SELECT(ALU__SELECT), .COUNTER_CLEAR(COUNTER_CLEAR), .LOAD(LOAD),
    .RM_ENABLE(RM_ENABLE), .MUXB_ENABLE(MUXB_ENABLE), .STORE(STORE), .RZ_ENABLE(RZ_ENABLE),
    .MUXB_SELECT(MUXB_SELECT), .STAGE_1(STAGE_1), .ADD(ADD), .RY_ENABLE(RY_ENABLE),
    .MUXY_ENABLE(MUXY_ENABLE), .STAGE_2(STAGE_2), .STAGE_3(STAGE_3), .ADI(ADI),
    .RA_ENABLE_SELECT(RA_ENABLE_SELECT), .MUXY_SELECT(MUXY_SELECT), .STAGE_4(STAGE_4), .SUB(SUB),
    .RB_ENABLE_SELECT(RB_ENABLE_SELECT), .MUXMEM_SELECT(MUXMEM_SELECT), .STAGE_5(STAGE_5), .SUI(SUI),
    .RY_ENABLE_SELECT(RY_ENABLE_SELECT), .PC_ENABLE(PC_ENABLE), .AND(AND), .IR_ENABLE(IR_ENABLE),
    .MEM_READ(MEM_READ), .ANI(ANI), .MEM_WRITE(MEM_WRITE), .PC_STOP(PC_STOP), .OR(OR),
    .MUX_STORE_SELECT(MUX_STORE_SELECT), .ORI(ORI), .HLT(HLT));
  Clock clock_1 (.out(CLK));

  // Notes on the sheet:
  //   KAUSHIK DEY
  //   20CS01043 - SEMESTER 5
  //   COA LAB - MINI PROJECT
  //   MAIN CIRCUIT
endmodule

module CU (
  input  CLK,
  input  MOV,
  input  ALU_ENABLE,
  input  [3:0] OPCODE,
  input  MVI,
  input  [2:0] ALU_SELECT,
  input  COUNTER_CLEAR,
  input  LOAD,
  input  MUXB_ENABLE,
  input  STORE,
  input  MUXB_SELECT,
  input  ADD,
  input  MUXY_ENABLE,
  input  ADI,
  input  MUXY_SELECT,
  input  SUB,
  input  MUXMEM_SELECT,
  input  SUI,
  input  PC_ENABLE,
  input  AND,
  input  MEM_READ,
  input  ANI,
  input  PC_STOP,
  input  OR,
  input  ORI,
  input  HLT,
  output RA_ENABLE,
  output RB_ENABLE,
  output RM_ENABLE,
  output RZ_ENABLE,
  output STAGE_1,
  output RY_ENABLE,
  output STAGE_2,
  output STAGE_3,
  output RA_ENABLE_SELECT,
  output STAGE_4,
  output RB_ENABLE_SELECT,
  output STAGE_5,
  output RY_ENABLE_SELECT,
  output IR_ENABLE,
  output MEM_WRITE,
  output MUX_STORE_SELECT
);

  wire and_10_out, or_5_out, TYPE_1, TYPE_2, TYPE_3, TYPE_4;
  wire [2:0] counter_1_q;

  Decoder #(.select(3), .enable("false")) decoder_1 (
    .out0(STAGE_1), .out1(STAGE_2), .out2(STAGE_3), .out3(STAGE_4), .out4(STAGE_5), .sel(counter_1_q));  // open: out5, out6, out7
  Counter #(.width(3), .max('h7)) counter_1 (
    .D(3'b000), .Q(counter_1_q), .clk(CLK), .clr(COUNTER_CLEAR));  // open: load, count, carry
  or or_1 (TYPE_1, ADD, ADI, SUB, SUI, AND, ANI, OR, ORI, MOV, MVI, LOAD, STORE);
  or or_2 (TYPE_2, LOAD, MOV, ADI, SUI, ANI, ORI);
  or or_3 (TYPE_3, ADD, SUB, AND, OR, STORE);
  or or_4 (TYPE_4, ADD, ADI, SUB, SUI, AND, ANI, HLT, OR, ORI, MOV, MVI, LOAD, STORE);
  and and_1 (PC_ENABLE, STAGE_1, TYPE_1);
  and and_2 (MUXY_ENABLE, STAGE_4, TYPE_1);
  and and_3 (MUXMEM_SELECT, STAGE_4, or_5_out);
  or or_5 (or_5_out, STORE, LOAD);
  and and_4 (MUXY_SELECT, STAGE_4, LOAD);
  and and_5 (MEM_WRITE, STAGE_4, STORE);
  and and_6 (MEM_READ, STAGE_1, TYPE_4);
  and and_7 (MUX_STORE_SELECT, STAGE_2, STORE);
  and and_8 (PC_STOP, STAGE_2, HLT);
  and and_9 (RB_ENABLE, STAGE_2, TYPE_3);
  and and_10 (and_10_out, STAGE_2, TYPE_2);
  or or_6 (RA_ENABLE, RB_ENABLE, and_10_out);
  and and_11 (RY_ENABLE_SELECT, STAGE_5, TYPE_1);
  and and_12 (ALU_ENABLE, STAGE_3, TYPE_1);
  and and_13 (MUXB_SELECT, STAGE_3, TYPE_2);
  and and_14 (RM_ENABLE, STAGE_3, STORE);

  assign IR_ENABLE = PC_ENABLE;
  assign MUXB_ENABLE = ALU_ENABLE;
  assign OPCODE[2:0] = ALU_SELECT;
  assign RA_ENABLE_SELECT = RA_ENABLE;
  assign RB_ENABLE_SELECT = RB_ENABLE;
  assign RY_ENABLE = MUXY_ENABLE;
  assign RZ_ENABLE = ALU_ENABLE;

  // Other names for the same wires on the sheet: Stage1 = STAGE_1; Stage2 = STAGE_2; Stage3 = STAGE_3;
  //   Stage4 = STAGE_4; Stage5 = STAGE_5

  // Notes on the sheet:
  //   OPCODES
  //   STAGE COUNTER
  //   CONTROL UNIT
  //   SIGNALS
  //   STAGE 1
  //   STAGE 4
  //   INSTRUCTION FETCHING
  //   STAGE 2
  //   STAGE 5
  //   MISC
  //   STAGE 3
endmodule

module ALU (
  input  [1:0] OPCODE,
  input  [31:0] INPUT_A,
  input  [31:0] OUTPUT,
  input  [31:0] INPUT_B
);

  wire [31:0] AND, DIFF, OR, SUM;

  Adder #(.width(32)) adder_1 (.a(INPUT_A), .b(INPUT_B), .out(SUM), .cin(1'b0));  // open: cout
  assign OR = INPUT_A | INPUT_B;  // OR_Gate or_1, 32 bits wide
  Subtractor #(.width(32)) subtractor_1 (.a(INPUT_A), .b(INPUT_B), .out(DIFF), .bin(1'b0));  // open: bout
  assign AND = INPUT_A & INPUT_B;  // AND_Gate and_1, 32 bits wide
  Multiplexer #(.select(2), .width(32), .enable("false")) multiplexer_1 (
    .in0(AND), .in1(OR), .in2(SUM), .in3(DIFF), .out(OUTPUT), .sel(OPCODE));

  // Other names for the same wires on the sheet: IN_A[31:0] = INPUT_A; IN_B[31:0] = INPUT_B; RES[31:0] = OUTPUT

  // Notes on the sheet:
  //   ARITHMETIC OPERATIONS
  //   LOGICAL OPERATIONS
  //   ARITHMETIC AND LOGIC UNIT
  //   OPERATION DECODER
endmodule

module RF (
  input  ENABLE_WRITE,
  input  [31:0] DATA_IN,
  input  CLOCK,
  input  CLEAR,
  input  [31:0] RA_OUT,
  input  [2:0] SELECT_RA,
  input  [2:0] SELECT_RB,
  input  [2:0] SELECT_RO,
  input  [31:0] RB_OUT
);

  wire EN_R1, EN_R2, EN_R3, EN_R4, EN_R5, EN_R6, EN_R7, EN_R8;
  wire [31:0] R1_OUT, R2_OUT, R3_OUT, R4_OUT, R5_OUT, R6_OUT, R7_OUT, R8_OUT;

  Register #(.width(32)) register_1 (.D(DATA_IN), .en(EN_R1), .Q(R1_OUT), .clk(CLOCK), .clr(CLEAR));
  Register #(.width(32)) register_2 (.D(DATA_IN), .en(EN_R3), .Q(R3_OUT), .clk(CLOCK), .clr(CLEAR));
  Register #(.width(32)) register_3 (.D(DATA_IN), .en(EN_R5), .Q(R5_OUT), .clk(CLOCK), .clr(CLEAR));
  // Probe on R1_OUT
  // Probe on R2_OUT
  // Probe on R3_OUT
  // Probe on R4_OUT
  // Probe on R5_OUT
  // Probe on R6_OUT
  // Probe on R7_OUT
  // Probe on R8_OUT
  Register #(.width(32)) register_4 (.D(DATA_IN), .en(EN_R2), .Q(R2_OUT), .clk(CLOCK), .clr(CLEAR));
  Register #(.width(32)) register_5 (.D(DATA_IN), .en(EN_R4), .Q(R4_OUT), .clk(CLOCK), .clr(CLEAR));
  Register #(.width(32)) register_6 (.D(DATA_IN), .en(EN_R6), .Q(R6_OUT), .clk(CLOCK), .clr(CLEAR));
  Register #(.width(32)) register_7 (.D(DATA_IN), .en(EN_R7), .Q(R7_OUT), .clk(CLOCK), .clr(CLEAR));
  Register #(.width(32)) register_8 (.D(DATA_IN), .en(EN_R8), .Q(R8_OUT), .clk(CLOCK), .clr(CLEAR));
  Multiplexer #(.select(3), .width(32), .enable("false")) multiplexer_1 (
    .in0(R1_OUT), .in1(R2_OUT), .in2(R3_OUT), .in3(R4_OUT), .in4(R5_OUT), .in5(R6_OUT), .in6(R7_OUT),
    .in7(R8_OUT), .out(RA_OUT), .sel(SELECT_RA));
  Demultiplexer #(.select(3), .enable("false")) demultiplexer_1 (
    .out0(EN_R1), .out1(EN_R2), .out2(EN_R3), .out3(EN_R4), .out4(EN_R5), .out5(EN_R6), .out6(EN_R7),
    .out7(EN_R8), .in(ENABLE_WRITE), .sel(SELECT_RO));
  Multiplexer #(.select(3), .width(32), .enable("false")) multiplexer_2 (
    .in0(R1_OUT), .in1(R2_OUT), .in2(R3_OUT), .in3(R4_OUT), .in4(R5_OUT), .in5(R6_OUT), .in6(R7_OUT),
    .in7(R8_OUT), .out(RB_OUT), .sel(SELECT_RB));

  // Other names for the same wires on the sheet: CLK = CLOCK; CLR = CLEAR; EN_WRITE = ENABLE_WRITE; RA[31:0] = RA_OUT;
  //   RB[31:0] = RB_OUT; RIN[31:0] = DATA_IN; SEL_RA[2:0] = SELECT_RA; SEL_RB[2:0] = SELECT_RB;
  //   SEL_RO[2:0] = SELECT_RO

  // Notes on the sheet:
  //   REGISTER FILE
  //   REGISTER PROBES
  //   RA SELECT
  //   WRITE SELECT
  //   RB SELECT
endmodule

module MU (
  input  [15:0] IN_ADDRESS,
  input  [31:0] OUT_DATA,
  input  [31:0] IN_DATA,
  input  WRITE_ENABLE,
  input  CLEAR,
  input  CLOCK,
  input  READ_ENABLE
);

  RAM #(.addrWidth(16), .dataWidth(32), .bus("separate")) ram_1 (
    .addr(IN_ADDRESS), .din(IN_DATA), .data(OUT_DATA), .str(WRITE_ENABLE), .sel(1'b1), .clk(CLOCK),
    .ld(READ_ENABLE), .clr(CLEAR));

  // Notes on the sheet:
  //   MEMORY UNIT
endmodule

module IAG (
  input  CLOCK,
  input  PC_ENABLE,
  input  PC_ENABLE_2,
  input  MUXPC_SELECT,
  input  CLEAR,
  input  [31:0] in_6,
  output [15:0] PC
);

  wire [15:0] adder_1_out, bit_extender_1_out, multiplexer_1_out;

  Bit_Extender #(.in_width(32)) bit_extender_1 (.in(in_6), .out(bit_extender_1_out));
  Multiplexer #(.width(16), .enable("false")) multiplexer_1 (
    .in0(bit_extender_1_out), .in1(adder_1_out), .out(multiplexer_1_out), .sel(MUXPC_SELECT));
  Register #(.width(16)) u_PC (.D(multiplexer_1_out), .en(PC_ENABLE), .Q(PC), .clk(CLOCK), .clr(CLEAR));
  Adder #(.width(16)) adder_1 (.a(PC), .b(16'h1), .out(adder_1_out));  // open: cin, cout

  assign PC_ENABLE_2 = PC_ENABLE;

  // Other names for the same wires on the sheet: CLK = CLOCK; RZ[31:0] = in_6

  // Notes on the sheet:
  //   INSTRUCTION ADDRESS GENERATOR
endmodule
